# Fritzing sketch typing-challenge (saved by Fritzing 0.9.6b)
breadboards: 1

parts:
  Part1 = Arduino Uno (Rev3)
  X1 = USB Connectors [package=usb-microb]
  Part2 = Arduino MicroSD Shield
  VCC1 = Battery
  VCC2 = Battery
  VCC3 = Battery
  S1 = Pushbutton [package=THT]

nets:
  N1: Part1.A0, Part2.A0
  N2: Part1.A1, Part2.A1
  N3: Part1.A2, Part2.A2
  N4: Part1.A3, Part2.A3
  N5: Part1.A4/SDA, Part2.A4
  N6: Part1.A5/SCL, Part2.A5
  N7: Part1.D9_PWM, Part2.D9
  N8: Part1.D10_PWM/SS, Part2.D10
  N9: Part1.D11_PWM/MOSI, Part2.MOSI
  N10: Part1.D12/MISO, Part2.MISO
  N11: Part1.D13/SCK, Part2.SCK
  N12: Part1.AREF, Part2.AREF
  N13: Part1.D0/RX, Part2.RX
  N14: Part1.D1/TX, Part2.TX
  N15: Part1.D2, X1.VBUS, Part2.D2
  N16: Part1.D3_PWM, X1.D-, Part2.D3
  N17: Part1.D4, Part2.D4
  N18: Part1.D5_PWM, Part2.D5
  N19: Part1.D6_PWM, Part2.D6
  N20: Part1.D7, Part2.D7
  N21: Part1.RESET, Part2.RES
  3V3: Part1.3V3, Part2.3.3V
  5V: Part1.5V, X1.D+, Part2.5V
  GND: Part1.GND, X1.GND, VCC3.-
  VIN: Part1.VIN, Part2.VIN, S1.leg1
  N22: VCC1.-, VCC2.+
  N23: VCC1.+, S1.leg0
  N24: VCC2.-, VCC3.+
